# Fritzing sketch circuit (saved by Fritzing 0.9.4)
circuit board: 15cm x 10cm
breadboards: 2

parts:
  Teensy_3_5 = Teensy 3.6 (Basic)
  part = shrouded pin header, 10 pins [form="♂ (shrouded male)"]
  J1 = shrouded pin header, 10 pins [form="♂ (shrouded male)"]
  W65C02 = IC, DIP package, 40 pins [chip_label=W65C02]
  C1 = Pad [width=1.2543313358024621 height=1.5052008641975383 connect=center]
  C2 = Pad [width=1.2543313358024621 height=1.5052008641975383 connect=center]
  part_2 = Pad [width=1.2543313358024621 height=1.5052008641975383 connect=center]
  part_3 = Pad [width=1.2543313358024621 height=1.5052008641975383 connect=center]

nets:
  N1: Teensy_3_5.D0, part.pin10, J1.pin10
  N2: Teensy_3_5.D1, part.pin9, J1.pin9
  N3: Teensy_3_5.D2, part.pin8, J1.pin8
  N4: Teensy_3_5.D3, part.pin7, J1.pin7
  N5: Teensy_3_5.D4, part.pin6, J1.pin6
  N6: Teensy_3_5.D5, part.pin5, J1.pin5
  N7: Teensy_3_5.D6, part.pin4, J1.pin4
  N8: Teensy_3_5.D7, W65C02.pin6
  N9: Teensy_3_5.D8, Teensy_3_5.D9, W65C02.pin37
  N10: Teensy_3_5.D11, part.pin3, J1.pin3
  N11: Teensy_3_5.D12, W65C02.pin2
  N12: Teensy_3_5.D13, W65C02.pin19
  N13: Teensy_3_5.A0/D14, W65C02.pin18
  N14: Teensy_3_5.A1/D15, W65C02.pin17
  N15: Teensy_3_5.A2/D16, W65C02.pin16
  N16: Teensy_3_5.A3/D17, W65C02.pin15
  N17: Teensy_3_5.A4/D18, W65C02.pin14
  N18: Teensy_3_5.A5/D19, W65C02.pin13
  N19: Teensy_3_5.A6/D20, W65C02.pin12
  N20: Teensy_3_5.A7/D21, W65C02.pin11
  N21: Teensy_3_5.A8/D22, W65C02.pin10
  N22: Teensy_3_5.A9/D23, W65C02.pin9
  N23: Teensy_3_5.3V3, Teensy_3_5.3V3_1, W65C02.pin8, W65C02.pin36, W65C02.pin38, part_2.pad, part_3.pad
  N24: Teensy_3_5.D24, W65C02.pin4
  N25: Teensy_3_5.D25, W65C02.pin33
  N26: Teensy_3_5.D26, W65C02.pin32
  N27: Teensy_3_5.D27, W65C02.pin31
  N28: Teensy_3_5.D28, W65C02.pin30
  N29: Teensy_3_5.D29, W65C02.pin29
  N30: Teensy_3_5.D30, W65C02.pin28
  N31: Teensy_3_5.D31, W65C02.pin27
  N32: Teensy_3_5.D32, W65C02.pin26
  N33: Teensy_3_5.D33, W65C02.pin40
  N34: Teensy_3_5.D34, W65C02.pin34
  N35: Teensy_3_5.D35, W65C02.pin25
  N36: Teensy_3_5.D36, W65C02.pin24
  N37: Teensy_3_5.D37, W65C02.pin23
  N38: Teensy_3_5.D38, W65C02.pin22
  N39: Teensy_3_5.D39, W65C02.pin20
  N40: Teensy_3_5.GND1, W65C02.pin21, C1.pad, C2.pad

notes:
  6502 PC
  Eric Wimberley
  Rev. 1.2

custom parts:
  Teensy 3.6 (Basic): The Teensy is a complete USB-based microcontoller development system, in a very small footprint, capable of implementing many types of projects. All programming is done via the USB port. No special programmer is needed, only a standard micro-USB cable and a PC or Macintosh with a USB port.
